# Fritzing sketch PingPong2022 (saved by Fritzing 0.9.10b)
circuit board: 16.311cm x 10.1534cm

parts:
  Teensy5 = Teensy 4.1
  Teensy2 = Teensy 4.1
  D1 = Rectifier Diode [part_number=1N4001 package="300 mil [THT]"]
  Piezo_Right = female pin header, 3 pins [form="♀ (female)"]
  Piezo_Left = female pin header, 3 pins [form="♀ (female)"]
  Piezo_Netz = female pin header, 3 pins [form="♀ (female)"]
  R3 = Resistor [tolerance=±5% resistance=220 power=0.25 package=THT]
  R4 = Resistor [tolerance=±5% resistance=220 power=0.25 package=THT]
  R5 = Resistor [tolerance=±5% resistance=220 power=0.25 package=THT]
  D3 = Rectifier Diode [part_number=1N4001 package="300 mil [THT]"]
  D4 = Rectifier Diode [part_number=1N4001 package="300 mil [THT]"]
  D5 = Rectifier Diode [part_number=1N4001 package="300 mil [THT]"]
  D6 = Rectifier Diode [part_number=1N4001 package="300 mil [THT]"]
  D7 = Rectifier Diode [part_number=1N4001 package="300 mil [THT]"]
  R6 = Resistor [tolerance=±5% resistance=220 power=0.25 package=THT]
  R7 = Resistor [tolerance=±5% resistance=220 power=0.25 package=THT]
  R8 = Resistor [tolerance=±5% resistance=220 power=0.25 package=THT]
  R9 = Resistor [tolerance=±5% resistance=220 power=0.25 package=THT]
  Bauteil1 = NRF24L01+ Tiny Module
  Right_Racket = NRF24L01+ Tiny Module
  Teensy4 = Teensy 4.1
  J6 = female pin header, 9 pins [form="♀ (female)"]
  J7 = female pin header, 9 pins [form="♀ (female)"]
  ZCD = female pin header, 3 pins [form="♀ (female)"]
  J9 = female pin header, 3 pins [form="♀ (female)"]
  J10 = female pin header, 3 pins [form="♀ (female)"]
  J11 = female pin header, 3 pins [form="♀ (female)"]
  J12 = female pin header, 3 pins [form="♀ (female)"]
  J13 = female pin header, 3 pins [form="♀ (female)"]
  J5 = female pin header, 6 pins [form="♀ (female)"]
  J15 = female pin header, 3 pins [form="♀ (female)"]
  J16 = female pin header, 3 pins [form="♀ (female)"]
  Pad1 = Pad [width=7.902222222222222 height=9.03111111111111 connect=center]
  Pad2 = Pad [width=7.902222222222222 height=9.03111111111111 connect=center]
  J17 = female pin header, 3 pins [form="♀ (female)"]
  J18 = female pin header, 3 pins [form="♀ (female)"]
  J19 = female pin header, 3 pins [form="♀ (female)"]
  J20 = female pin header, 3 pins [form="♀ (female)"]
  J21 = female pin header, 3 pins [form="♀ (female)"]
  J22 = female pin header, 3 pins [form="♀ (female)"]

nets:
  GND: Teensy5.GND, Teensy5.GND2#55, R3.Pin_1, D3.cathode, D6.anode, R6.Pin_1, Bauteil1.GND, Right_Racket.GND, Teensy4.GND, Teensy4.GND2, J9.pin2, J10.pin2, J11.pin2, J12.pin2, J15.pin3, J16.pin2, Pad2.pad, J17.pin1
  N1: Teensy5.D2, J9.pin3
  N2: Teensy5.D3, J10.pin3
  N3: Teensy5.D4, J11.pin3
  N4: Teensy5.D5, J12.pin3
  N5: Teensy5.D11, Bauteil1.MOSI, Right_Racket.MOSI
  N6: Teensy5.D12, Bauteil1.MISO, Right_Racket.MISO
  N7: Teensy5.D13, Bauteil1.SCK, Right_Racket.SCK
  N8: Teensy5.A0/D14, Teensy2.D0
  N9: Teensy5.A2/D16, Teensy4.A10/D24
  N10: Teensy5.A3/D17, Teensy4.A11/D25
  VCC: Teensy5.3V3_LOW, D1.cathode, D6.cathode, D7.cathode, Bauteil1.VCC, Right_Racket.VCC
  N11: Teensy5.GND2#31, Teensy2.GND
  VIN: Teensy5.Vin, Teensy2.Vin, Teensy4.Vin, ZCD.pin1, J9.pin1, J10.pin1, J11.pin1, J12.pin1, J13.pin3, J16.pin1, Pad1.pad
  N12: Teensy5.A10/D24, Teensy2.A10/D24
  N13: Teensy5.A11/D25, Teensy2.A11/D25
  N14: Teensy5.A12/D26, R9.Pin_1
  N15: Teensy5.A13/D27, J15.pin1
  N16: Teensy5.D29, Teensy4.D0
  N17: Teensy5.D31, Bauteil1.CE
  N18: Teensy5.D32, Bauteil1.CS
  N19: Teensy5.D37, Right_Racket.CE
  N20: Teensy5.A14/D38, Right_Racket.CS
  N21: Teensy5.A15/D39, R5.Pin_1, D5.cathode, D7.anode, R8.Pin_1
  N22: Teensy5.A16/D40, D1.anode, R4.Pin_1, D4.cathode, R7.Pin_1
  N23: Teensy2.D1, J16.pin3
  N24: Teensy2.D2, ZCD.pin3
  N25: Teensy2.D3, J6.pin8
  N26: Teensy2.D4, J6.pin7
  N27: Teensy2.D5, J6.pin6
  N28: Teensy2.A0/D14, J6.pin2
  N29: Teensy2.A1/D15, J6.pin3
  N30: Teensy2.A2/D16, J6.pin4
  N31: Teensy2.A3/D17, J6.pin5
  N32: Teensy2.A8/D22, J6.pin9
  N33: Teensy2.GND2, Teensy4.A17/D41, ZCD.pin2, J13.pin1, J17.pin2, J18.pin2, J19.pin2, J20.pin2, J21.pin2, J22.pin2
  N34: Teensy2.D28, Teensy4.A13/D27
  N35: Teensy2.D29, Teensy4.D28
  N36: Teensy2.D33, J7.pin1
  N37: Teensy2.D34, J7.pin2
  N38: Teensy2.D35, J7.pin3
  N39: Teensy2.D36, J7.pin4
  N40: Teensy2.D37, J7.pin5
  N41: Teensy2.A14/D38, J7.pin6
  N42: Teensy2.A15/D39, J7.pin7
  N43: Teensy2.A16/D40, J7.pin8
  N44: Teensy2.A17/D41, Piezo_Right.pin1, Piezo_Left.pin1, Piezo_Netz.pin1, D3.anode, D4.anode, D5.anode, R6.Pin_0, R7.Pin_0, R8.Pin_0, J6.pin1, J7.pin9
  N45: Piezo_Right.pin3, R3.Pin_0
  N46: Piezo_Left.pin3, R5.Pin_0
  N47: Piezo_Netz.pin3, R4.Pin_0
  N48: R9.Pin_0, J15.pin2
  N49: Teensy4.3V3_LOW, J17.pin3
  N50: Teensy4.D30, J5.pin4
  N51: Teensy4.D31, J5.pin6
  N52: Teensy4.D32, J5.pin5
  N53: Teensy4.D33, J5.pin1
  N54: Teensy4.D34, J5.pin2
  N55: Teensy4.D35, J5.pin3
  N56: Teensy4.D36, J22.pin1
  N57: Teensy4.D37, J21.pin1
  N58: Teensy4.A14/D38, J20.pin1
  N59: Teensy4.A15/D39, J19.pin1
  N60: Teensy4.A16/D40, J18.pin1

notes:
  Gluehbirnen
  MOTORS
  NRF24
  PIEZOS
  LED-STRIP
  IC2
  +
  -

custom parts:
  Teensy 4.1: The Teensy is a complete USB-based microcontoller development system, in a very small footprint, capable of implementing many types of projects. All programming is done via the USB port. No special programmer is needed, only a standard micro-USB cable and a PC or Macintosh with a USB port.
  NRF24L01+ Tiny Module: This module stamp is for the Nordic Semiconductor NRF24L01+ 2.4GHz RF transceiver IC. Origined from Richard Bruneau, Fabian Althaus. 2021: PCB part Modified by Po Ting Chen, Panda'Spectrum of Taiwan, for tiny footprint module. ask fb.me/pandaspectrum for details ver_2 - with breadboard edit
