# Fritzing sketch PingPong2022.gzz (saved by Fritzing 0.9.10b)
circuit board: 15.6109cm x 9.85278cm

parts:
  Teensy5 = Teensy 4.1
  Teensy2 = Teensy 4.1
  D1 = Rectifier Diode [part_number=1N4001 package="300 mil [THT]"]
  Piezo_Right = female pin header, 3 pins [form="♀ (female)"]
  Piezo_Left = female pin header, 3 pins [form="♀ (female)"]
  Piezo_Netz = female pin header, 3 pins [form="♀ (female)"]
  R3 = Resistor [tolerance=±5% resistance=220 power=0.25 package=THT]
  R4 = Resistor [tolerance=±5% resistance=220 power=0.25 package=THT]
  R5 = Resistor [tolerance=±5% resistance=220 power=0.25 package=THT]
  D3 = Rectifier Diode [part_number=1N4001 package="300 mil [THT]"]
  D4 = Rectifier Diode [part_number=1N4001 package="300 mil [THT]"]
  D5 = Rectifier Diode [part_number=1N4001 package="300 mil [THT]"]
  D6 = Rectifier Diode [part_number=1N4001 package="300 mil [THT]"]
  D7 = Rectifier Diode [part_number=1N4001 package="300 mil [THT]"]
  R6 = Resistor [tolerance=±5% resistance=220 power=0.25 package=THT]
  R7 = Resistor [tolerance=±5% resistance=220 power=0.25 package=THT]
  R8 = Resistor [tolerance=±5% resistance=220 power=0.25 package=THT]
  R9 = Resistor [tolerance=±5% resistance=220 power=0.25 package=THT]
  Bauteil1 = NRF24L01+ Tiny Module
  Right_Racket = NRF24L01+ Tiny Module
  Teensy4 = Teensy 4.1
  J6 = female pin header, 9 pins [form="♀ (female)"]
  J7 = female pin header, 9 pins [form="♀ (female)"]
  ZCD = female pin header, 3 pins [form="♀ (female)"]
  J9 = female pin header, 3 pins [form="♀ (female)"]
  J10 = female pin header, 3 pins [form="♀ (female)"]
  J11 = female pin header, 3 pins [form="♀ (female)"]
  J12 = female pin header, 3 pins [form="♀ (female)"]
  J13 = female pin header, 3 pins [form="♀ (female)"]
  J5 = female pin header, 6 pins [form="♀ (female)"]
  J15 = female pin header, 3 pins [form="♀ (female)"]
  J16 = female pin header, 3 pins [form="♀ (female)"]
  Pad1 = Pad [width=7.902222222222222 height=9.03111111111111 connect=center]
  Pad2 = Pad [width=7.902222222222222 height=9.03111111111111 connect=center]
  J17 = female pin header, 3 pins [form="♀ (female)"]
  J18 = female pin header, 3 pins [form="♀ (female)"]
  J19 = female pin header, 3 pins [form="♀ (female)"]
  J20 = female pin header, 3 pins [form="♀ (female)"]
  J21 = female pin header, 3 pins [form="♀ (female)"]
  J22 = female pin header, 3 pins [form="♀ (female)"]

nets:
  GND: Teensy5.GND, Teensy5.GND2, Teensy2.GND, Teensy2.GND2, Teensy2.A17/D41, Piezo_Right.pin1, Piezo_Left.pin1, Piezo_Netz.pin1, R3.Pin_1, D3.cathode, D3.anode, D4.anode, D5.anode, D6.anode, R6.Pin_0, R6.Pin_1, R7.Pin_0, R8.Pin_0, Bauteil1.GND, Right_Racket.GND, Teensy4.GND, Teensy4.A17/D41, Teensy4.GND2, J6.pin1, J7.pin9, ZCD.pin2, J9.pin1, J10.pin1, J11.pin1, J12.pin1, J13.pin1, J15.pin3, J16.pin2, Pad2.pad, J17.pin1, J17.pin2, J18.pin2, J19.pin2, J20.pin2, J21.pin2, J22.pin2
  N1: Teensy5.D0, Teensy4.D1
  N2: Teensy5.D1, Teensy4.D0
  N3: Teensy5.D2, J9.pin3
  N4: Teensy5.D3, J10.pin3
  N5: Teensy5.D4, J11.pin3
  N6: Teensy5.D5, J12.pin3
  N7: Teensy5.D11, Bauteil1.MOSI, Right_Racket.MOSI
  N8: Teensy5.D12, Bauteil1.MISO, Right_Racket.MISO
  N9: Teensy5.D13, Bauteil1.SCK, Right_Racket.SCK
  VCC: Teensy5.3V3_LOW, D1.cathode, D6.cathode, D7.cathode, Bauteil1.VCC, Right_Racket.VCC, J9.pin2, J10.pin2, J11.pin2, J12.pin2
  N10: Teensy5.A10/D24, Teensy2.A10/D24
  N11: Teensy5.A11/D25, Teensy2.A11/D25
  N12: Teensy5.A12/D26, R9.Pin_1
  N13: Teensy5.A13/D27, J15.pin1
  N14: Teensy5.D31, Bauteil1.CE
  N15: Teensy5.D32, Bauteil1.CS
  N16: Teensy5.D34, Teensy2.D35
  N17: Teensy5.D35, Teensy2.D34
  N18: Teensy5.D37, Right_Racket.CE
  N19: Teensy5.A14/D38, Right_Racket.CS
  N20: Teensy5.A15/D39, R5.Pin_1, D5.cathode, D7.anode, R8.Pin_1
  N21: Teensy5.A16/D40, D1.anode, R4.Pin_1, D4.cathode, R7.Pin_1
  N22: Teensy2.D1, J16.pin3
  N23: Teensy2.D2, ZCD.pin3
  N24: Teensy2.D3, J6.pin8
  N25: Teensy2.D4, J6.pin7
  N26: Teensy2.D5, J6.pin6
  N27: Teensy2.A0/D14, J6.pin2
  N28: Teensy2.A1/D15, J6.pin3
  N29: Teensy2.A2/D16, J6.pin4
  N30: Teensy2.A3/D17, J6.pin5
  N31: Teensy2.A8/D22, J6.pin9
  VIN: Teensy2.Vin, Teensy4.Vin, ZCD.pin1, J13.pin3, J16.pin1, Pad1.pad
  N32: Teensy2.D28, Teensy4.A13/D27
  N33: Teensy2.D29, Teensy4.D28
  N34: Teensy2.D30, J7.pin3
  N35: Teensy2.D31, J7.pin2
  N36: Teensy2.D32, J7.pin1
  N37: Teensy2.D36, J7.pin4
  N38: Teensy2.D37, J7.pin5
  N39: Teensy2.A14/D38, J7.pin6
  N40: Teensy2.A15/D39, J7.pin7
  N41: Teensy2.A16/D40, J7.pin8
  N42: Piezo_Right.pin3, R3.Pin_0
  N43: Piezo_Left.pin3, R5.Pin_0
  N44: Piezo_Netz.pin3, R4.Pin_0
  N45: R9.Pin_0, J15.pin2
  N46: Teensy4.3V3_LOW, J17.pin3
  N47: Teensy4.D30, J5.pin4
  N48: Teensy4.D31, J5.pin6
  N49: Teensy4.D32, J5.pin5
  N50: Teensy4.D33, J5.pin1
  N51: Teensy4.D34, J5.pin2
  N52: Teensy4.D35, J5.pin3
  N53: Teensy4.D36, J22.pin1
  N54: Teensy4.D37, J21.pin1
  N55: Teensy4.A14/D38, J20.pin1
  N56: Teensy4.A15/D39, J19.pin1
  N57: Teensy4.A16/D40, J18.pin1

notes:
  Gluehbirnen
  MOTORS
  NRF24
  PIEZOS
  LED-STRIP
  IC2
  +
  -
  5v
  SG
  3.3V
  GND
  Neopixel 4W
  5V
  SCK
  D-OUT
  Light Strip Sk9882
  Serial 1
  ZCD

custom parts:
  Teensy 4.1: The Teensy is a complete USB-based microcontoller development system, in a very small footprint, capable of implementing many types of projects. All programming is done via the USB port. No special programmer is needed, only a standard micro-USB cable and a PC or Macintosh with a USB port.
  NRF24L01+ Tiny Module: This module stamp is for the Nordic Semiconductor NRF24L01+ 2.4GHz RF transceiver IC. Origined from Richard Bruneau, Fabian Althaus. 2021: PCB part Modified by Po Ting Chen, Panda'Spectrum of Taiwan, for tiny footprint module. ask fb.me/pandaspectrum for details ver_2 - with breadboard edit
